// Digital circuit spingate.dig as structural Verilog
module spingate (
);

  wire _7400_1_pin1, _7400_1_pin2, _7400_1_pin3, _7400_1_pin4, _7400_1_pin6, _7400_1_pin8, _7400_1_pin10,
       _7400_1_pin12, _74157_1_pin3, _74157_1_pin4, _74157_1_pin5, _74157_1_pin6, _74157_1_pin9,
       _74157_1_pin14, _74164_1_pin3, _74164_1_pin4, _74164_1_pin5, _74164_1_pin6, _74164_1_pin10,
       _74164_1_pin11, _74164_1_pin12, _74164_1_pin13, _74164_2_pin3, _74164_2_pin4, _74164_2_pin5,
       _74164_2_pin6, _74164_2_pin10, _74164_2_pin11, _74164_2_pin12, _74175_1_pin12, and_1_out,
       button_1_out, dipswitch_1_out, dipswitch_2_out;

  DipSwitch dipswitch_1 (.out(dipswitch_1_out));
  DipSwitch dipswitch_2 (.out(dipswitch_2_out));
  and and_1 (and_1_out, dipswitch_2_out, button_1_out);
  Button button_1 (.out(button_1_out));
  _7400 _7400_1 (
    .pin1(_7400_1_pin1), .pin2(_7400_1_pin2), .pin3(_7400_1_pin3), .pin4(_7400_1_pin4), .pin5(_7400_1_pin3),
    .pin6(_7400_1_pin6), .pin7(1'b0), .pin8(_7400_1_pin8), .pin9(_7400_1_pin6), .pin10(_7400_1_pin10),
    .pin11(_7400_1_pin10), .pin12(_7400_1_pin12), .pin13(_7400_1_pin2), .pin14(1'b1));
  _74157 _74157_1 (
    .pin1(dipswitch_1_out), .pin2(_7400_1_pin1), .pin3(_74157_1_pin3), .pin4(_74157_1_pin4),
    .pin5(_74157_1_pin5), .pin6(_74157_1_pin6), .pin8(1'b0), .pin9(_74157_1_pin9), .pin10(_7400_1_pin12),
    .pin11(_7400_1_pin4), .pin12(_74157_1_pin3), .pin13(_7400_1_pin8), .pin14(_74157_1_pin14), .pin15(1'b0),
    .pin16(1'b1));  // open: pin7
  // NotConnected on _74157_1_pin5
  // NotConnected on _74157_1_pin6
  _74175 _74175_1 (
    .pin1(1'b1), .pin2(_7400_1_pin1), .pin4(_74157_1_pin4), .pin5(_74157_1_pin3), .pin7(_7400_1_pin2),
    .pin8(1'b0), .pin9(button_1_out), .pin12(_74175_1_pin12), .pin13(_74157_1_pin9), .pin14(_7400_1_pin12),
    .pin15(_7400_1_pin4), .pin16(1'b1));  // open: pin3, pin6, pin10, pin11
  LED led_1 (.in(_7400_1_pin4));
  LED led_2 (.in(_7400_1_pin12));
  LED led_3 (.in(_7400_1_pin1));
  // NotConnected on _74175_1_pin12
  Seven_Seg seven_seg_1 (
    .a(_74164_1_pin13), .b(_74164_1_pin12), .c(_74164_1_pin11), .d(_74164_1_pin10), .e(_74164_1_pin4),
    .f(_74164_1_pin5), .g(_74164_1_pin6), .dp(_74164_1_pin3));
  _74164 _74164_1 (
    .pin1(_7400_1_pin2), .pin2(1'b1), .pin3(_74164_1_pin3), .pin4(_74164_1_pin4), .pin5(_74164_1_pin5),
    .pin6(_74164_1_pin6), .pin7(1'b0), .pin8(and_1_out), .pin9(1'b1), .pin10(_74164_1_pin10),
    .pin11(_74164_1_pin11), .pin12(_74164_1_pin12), .pin13(_74164_1_pin13), .pin14(1'b1));
  LED led_4 (.in(_7400_1_pin2));
  LED led_5 (.in(_74164_1_pin3));
  LED led_6 (.in(_74164_1_pin4));
  LED led_7 (.in(_74164_1_pin5));
  LED led_8 (.in(_74164_1_pin6));
  LED led_9 (.in(_74157_1_pin14));
  _74164 _74164_2 (
    .pin1(_74164_1_pin6), .pin2(_74164_1_pin6), .pin3(_74164_2_pin3), .pin4(_74164_2_pin4),
    .pin5(_74164_2_pin5), .pin6(_74164_2_pin6), .pin7(1'b0), .pin8(and_1_out), .pin9(1'b1),
    .pin10(_74164_2_pin10), .pin11(_74164_2_pin11), .pin12(_74164_2_pin12), .pin13(_74157_1_pin14),
    .pin14(1'b1));
  LED led_10 (.in(_74164_2_pin12));
  LED led_11 (.in(_74164_2_pin11));
  LED led_12 (.in(_74164_2_pin3));
  LED led_13 (.in(_74164_2_pin4));
  LED led_14 (.in(_74164_2_pin10));
  LED led_15 (.in(_74164_2_pin5));
  LED led_16 (.in(_74164_2_pin6));

  // Notes on the sheet:
  //   accum <= gate ? data0` : accum
  //   phase <= gate ? NOT(phase) : phase
  //   data0 <= gate ? (phase ? NAND(accum, data0) : data0) : dataX
  //   MuxR
  //   NAND
  //   MuxO
  //   MuxW
  //   Data0`
  //   Accum`
  //   Phase`
  //   Phase
  //   Accum
  //   Data0
endmodule
